// Logisim project alu.circ as structural Verilog: 1 circuit, main circuit main
module main (
  input  Carry_in,
  input  INVA,
  input  A,
  input  ENA,
  input  B,
  input  ENB,
  input  F1,
  input  F0,
  output \output ,
  output Carry_out
);

  wire adder_1_out, and_1_out, and_2_out, and_3_out, and_4_out, and_5_out, and_6_out, and_7_out, and_8_out,
       and_9_out, and_10_out, and_11_out, not_1_out, not_2_out, not_3_out, or_1_out, xor_1_out;

  not not_1 (not_1_out, F0);
  and and_1 (and_1_out, A, ENA);
  and and_2 (and_2_out, B, ENB);
  not not_2 (not_2_out, F1);
  xor xor_1 (xor_1_out, INVA, and_1_out);
  and and_3 (and_3_out, not_1_out, not_2_out);
  and and_4 (and_4_out, not_1_out, F1);
  and and_5 (and_5_out, not_2_out, F0);
  and and_6 (and_6_out, F1, F0);
  and and_7 (and_7_out, xor_1_out, and_2_out);
  or or_1 (or_1_out, xor_1_out, and_2_out);
  not not_3 (not_3_out, and_2_out);
  and and_8 (and_8_out, and_7_out, and_3_out);
  and and_9 (and_9_out, and_4_out, or_1_out);
  and and_10 (and_10_out, not_3_out, and_5_out);
  Adder #(.width(1)) adder_1 (.a(xor_1_out), .b(and_2_out), .out(adder_1_out), .cin(Carry_in), .cout(Carry_out));
  and and_11 (and_11_out, adder_1_out, and_6_out);
  or or_2 (\output , and_8_out, and_9_out, and_10_out, and_11_out);
endmodule
